// Logisim project CPU.circ as structural Verilog: 7 circuits, main circuit main
module main (
  input  [3:0] in_1,
  input  in_2,
  input  in_3,
  input  WE_MAR,
  input  [7:0] in_5,
  input  count,
  input  OE_MAR,
  input  clr_counter,
  input  in_9,
  input  internal_OE,
  input  WE_RAM,
  input  OE_RAM,
  input  WE_MBR,
  input  WE_instruct_reg,
  input  OE_MBR,
  input  OE_instruct_reg,
  input  OE_alu,
  input  WE_A,
  input  OE_A,
  input  WE_O,
  input  OE_O,
  input  WE_B,
  input  OE_B,
  output [3:0] MAR_content,
  output [3:0] out_25,
  output [7:0] instruct_Reg_content,
  output [7:0] out_27,
  output [7:0] alu_output,
  output [7:0] reg_A_content,
  output [7:0] reg_B_content,
  output [7:0] output_reg_content
);

  wire clock_1_out;
  wire [3:0] controlled_buffer_1_out, MAR_dout;
  wire [7:0] alu_1_dout, instruction_register_dout;

  Clock clock_1 (.out(clock_1_out));
  // myCounter program_counter: pin names not known; wires that end beside it: count, clock_1_out, clr_counter, out_25
  eightbitregister instruction_register (
    .CLK(clock_1_out), .DIn(alu_1_dout), .WE(WE_instruct_reg), .OE(OE_instruct_reg),
    .Dout(instruction_register_dout), .storedData(instruct_Reg_content));
  ALU alu_1 (
    .REGA(reg_A_content), .REGB(reg_B_content), .OE(OE_alu), .Dout(alu_1_dout), .aluOutput(alu_output));  // open: Cout
  eightbitregister registerA (
    .CLK(clock_1_out), .DIn(alu_1_dout), .WE(WE_A), .OE(OE_A), .storedData(reg_A_content));  // open: Dout
  eightbitregister registerB (
    .CLK(clock_1_out), .DIn(alu_1_dout), .WE(WE_B), .OE(OE_B), .storedData(reg_B_content));  // open: Dout
  assign controlled_buffer_1_out = in_3 ? out_25 : 4'bz;  // Controlled_Buffer controlled_buffer_1
  BitSelector #(.group(4)) bitselector_1 (.in(instruction_register_dout), .out(controlled_buffer_1_out), .sel(1'b0));
  assign alu_1_dout = in_9 ? in_5 : 8'bz;  // Controlled_Buffer controlled_buffer_2
  LED led_1 (.in(alu_1_dout[7]));
  LED led_2 (.in(alu_1_dout[4]));
  LED led_3 (.in(alu_1_dout[3]));
  LED led_4 (.in(alu_1_dout[6]));
  LED led_5 (.in(alu_1_dout[5]));
  LED led_6 (.in(alu_1_dout[2]));
  LED led_7 (.in(alu_1_dout[1]));
  LED led_8 (.in(alu_1_dout[0]));
  memoryAddressRegister MAR (
    .CLK(clock_1_out), .DIn(controlled_buffer_1_out), .WE(WE_MAR), .OE(OE_MAR), .Dout(MAR_dout),
    .stored_data(MAR_content));
  assign alu_1_dout = internal_OE ? out_27 : 8'bz;  // Controlled_Buffer controlled_buffer_3
  eightbitregister MBR (
    .CLK(clock_1_out), .DIn(alu_1_dout), .WE(WE_MBR), .OE(OE_MBR), .Dout(alu_1_dout), .storedData(out_27));
  assign MAR_dout = in_2 ? in_1 : 4'bz;  // Controlled_Buffer controlled_buffer_4
  eightbitregister output_register (
    .CLK(clock_1_out), .DIn(alu_1_dout), .WE(WE_O), .OE(OE_O), .Dout(alu_1_dout),
    .storedData(output_reg_content));
  LED led_9 (.in(alu_1_dout[7]));
  LED led_10 (.in(alu_1_dout[6]));
  LED led_11 (.in(alu_1_dout[5]));
  LED led_12 (.in(alu_1_dout[4]));
  LED led_13 (.in(alu_1_dout[3]));
  LED led_14 (.in(alu_1_dout[2]));
  LED led_15 (.in(alu_1_dout[1]));
  LED led_16 (.in(alu_1_dout[0]));
  RAM #(.addrWidth(4)) ram_1 (
    .addr(MAR_dout), .we(WE_RAM), .oe(OE_RAM), .clk(clock_1_out), .din(alu_1_dout), .dout(alu_1_dout));

  // Notes on the sheet:
  //   Note:register A and register B are accumulation registers 
  //   opcode are as follows : 1. 0000 - load to reg A 
  //   2. 0001 - load to reg B
  //   3 . 0010 - ADD
  //   4. 0011 - STORE
  //   internal address bus
  //   internal data bus
  //   external address bus
  //   external data bus
endmodule

module memory_cell (
  input  DIn,
  input  CLK,
  input  CLR,
  input  WE,
  input  OE,
  output StoredData,
  output Dout
);

  wire and_1_out, and_2_out, not_1_out, or_1_out;

  and and_1 (and_1_out, StoredData, not_1_out);
  not not_1 (not_1_out, WE);
  and and_2 (and_2_out, DIn, WE);
  D_Flip_Flop d_ff_1 (.D(or_1_out), .clk(CLK), .Q(StoredData), .reset(CLR));  // open: Qn, preset
  or or_1 (or_1_out, and_1_out, and_2_out);
  assign Dout = OE ? StoredData : 1'bz;  // Controlled_Buffer controlled_buffer_1
endmodule

module eightbitregister (
  input  CLK,
  input  [7:0] DIn,
  input  WE,
  input  OE,
  output [7:0] Dout,
  output [7:0] storedData
);

  memory_cell memory_cell_1 (
    .DIn(DIn[1]), .CLK(CLK), .WE(WE), .OE(OE), .StoredData(storedData[1]), .Dout(Dout[1]));  // open: CLR
  memory_cell memory_cell_2 (
    .DIn(DIn[2]), .CLK(CLK), .WE(WE), .OE(OE), .StoredData(storedData[2]), .Dout(Dout[2]));  // open: CLR
  memory_cell memory_cell_3 (
    .DIn(DIn[3]), .CLK(CLK), .WE(WE), .OE(OE), .StoredData(storedData[3]), .Dout(Dout[3]));  // open: CLR
  memory_cell memory_cell_4 (
    .DIn(DIn[0]), .CLK(CLK), .WE(WE), .OE(OE), .StoredData(storedData[0]), .Dout(Dout[0]));  // open: CLR
  memory_cell memory_cell_5 (
    .DIn(DIn[4]), .CLK(CLK), .WE(WE), .OE(OE), .StoredData(storedData[4]), .Dout(Dout[4]));  // open: CLR
  memory_cell memory_cell_6 (
    .DIn(DIn[5]), .CLK(CLK), .WE(WE), .OE(OE), .StoredData(storedData[5]), .Dout(Dout[5]));  // open: CLR
  memory_cell memory_cell_7 (
    .DIn(DIn[6]), .CLK(CLK), .WE(WE), .StoredData(storedData[6]), .Dout(Dout[6]));  // open: CLR, OE
  memory_cell memory_cell_8 (
    .DIn(DIn[7]), .CLK(CLK), .WE(WE), .OE(OE), .StoredData(storedData[7]), .Dout(Dout[7]));  // open: CLR
endmodule

module memoryAddressRegister (
  input  CLK,
  input  [3:0] DIn,
  input  WE,
  input  OE,
  output [3:0] Dout,
  output [3:0] stored_data
);

  memory_cell memory_cell_1 (
    .DIn(DIn[1]), .CLK(CLK), .WE(WE), .OE(OE), .StoredData(stored_data[1]), .Dout(Dout[1]));  // open: CLR
  memory_cell memory_cell_2 (
    .DIn(DIn[2]), .CLK(CLK), .WE(WE), .OE(OE), .StoredData(stored_data[2]), .Dout(Dout[2]));  // open: CLR
  memory_cell memory_cell_3 (
    .DIn(DIn[3]), .CLK(CLK), .WE(WE), .OE(OE), .StoredData(stored_data[3]), .Dout(Dout[3]));  // open: CLR
  memory_cell memory_cell_4 (
    .DIn(DIn[0]), .CLK(CLK), .WE(WE), .OE(OE), .StoredData(stored_data[0]), .Dout(Dout[0]));  // open: CLR
endmodule

module ALU (
  input  [7:0] REGA,
  input  [7:0] REGB,
  input  OE,
  output [7:0] Dout,
  output Cout,
  output [7:0] aluOutput
);

  wire adder_1_cout;

  Adder adder_1 (.a(REGA), .b(REGB), .out(aluOutput), .cout(adder_1_cout));  // open: cin
  assign Dout = OE ? aluOutput : 8'bz;  // Controlled_Buffer controlled_buffer_1
endmodule

module program_counter (
  input  in_1,
  input  in_2,
  input  in_3,
  input  [1:0] in_4,
  input  in_5,
  input  WE_MAR,
  input  [7:0] in_7,
  input  OE_MAR,
  input  in_9,
  input  internal_OE,
  input  WE_MBR,
  input  WE_instruct_reg,
  input  OE_MBR,
  input  OE_instruct_reg,
  input  OE_alu,
  input  WE_A,
  input  OE_A,
  input  WE_O,
  input  OE_O,
  input  WE_B,
  input  OE_B,
  output [1:0] out_22,
  output [3:0] MAR_content,
  output [7:0] instruct_Reg_content,
  output [7:0] out_25,
  output [7:0] alu_output,
  output [7:0] reg_A_content,
  output [7:0] reg_B_content,
  output [7:0] output_reg_content
);

  wire clock_1_out;
  wire [3:0] bitselector_1_out, MAR_dout;
  wire [7:0] alu_1_dout, instruction_register_dout;

  Counter #(.max('h3), .width(2)) counter_1 (
    .clr(in_1), .load(in_2), .up(in_3), .clk(in_5), .D(in_4), .Q(out_22));  // open: count, carry
  Clock clock_1 (.out(clock_1_out));
  eightbitregister instruction_register (
    .CLK(clock_1_out), .DIn(alu_1_dout), .WE(WE_instruct_reg), .OE(OE_instruct_reg),
    .Dout(instruction_register_dout), .storedData(instruct_Reg_content));
  ALU alu_1 (
    .REGA(reg_A_content), .REGB(reg_B_content), .OE(OE_alu), .Dout(alu_1_dout), .aluOutput(alu_output));  // open: Cout
  eightbitregister registerA (
    .CLK(clock_1_out), .DIn(alu_1_dout), .WE(WE_A), .OE(OE_A), .storedData(reg_A_content));  // open: Dout
  eightbitregister registerB (
    .CLK(clock_1_out), .DIn(alu_1_dout), .WE(WE_B), .OE(OE_B), .storedData(reg_B_content));  // open: Dout
  BitSelector #(.group(4)) bitselector_1 (
    .in(instruction_register_dout),
    .out({bitselector_1_out[3], bitselector_1_out[1], bitselector_1_out[2], bitselector_1_out[0]}), .sel(1'b0));
  assign alu_1_dout = in_9 ? in_7 : 8'bz;  // Controlled_Buffer controlled_buffer_1
  LED led_1 (.in(alu_1_dout[7]));
  LED led_2 (.in(alu_1_dout[4]));
  LED led_3 (.in(alu_1_dout[3]));
  LED led_4 (.in(alu_1_dout[6]));
  LED led_5 (.in(alu_1_dout[5]));
  LED led_6 (.in(alu_1_dout[2]));
  LED led_7 (.in(alu_1_dout[1]));
  LED led_8 (.in(alu_1_dout[0]));
  memoryAddressRegister MAR (
    .CLK(clock_1_out), .DIn(bitselector_1_out), .WE(WE_MAR), .OE(OE_MAR), .Dout(MAR_dout),
    .stored_data(MAR_content));
  assign alu_1_dout = internal_OE ? out_25 : 8'bz;  // Controlled_Buffer controlled_buffer_2
  eightbitregister MBR (
    .CLK(clock_1_out), .DIn(alu_1_dout), .WE(WE_MBR), .OE(OE_MBR), .Dout(alu_1_dout), .storedData(out_25));
  eightbitregister output_register (
    .CLK(clock_1_out), .DIn(alu_1_dout), .WE(WE_O), .OE(OE_O), .Dout(alu_1_dout),
    .storedData(output_reg_content));
  LED led_9 (.in(alu_1_dout[7]));
  LED led_10 (.in(alu_1_dout[6]));
  LED led_11 (.in(alu_1_dout[5]));
  LED led_12 (.in(alu_1_dout[4]));
  LED led_13 (.in(alu_1_dout[3]));
  LED led_14 (.in(alu_1_dout[2]));
  LED led_15 (.in(alu_1_dout[1]));
  LED led_16 (.in(alu_1_dout[0]));

  // Notes on the sheet:
  //   internal address bus
  //   internal data bus
  //   external address bus
  //   external data bus
endmodule

module myCounter (
  input  [3:0] INP,
  input  increment,
  input  CLK,
  output [3:0] out_4
);

  wire t_ff_1_qn, t_ff_2_qn, t_ff_3_qn;

  T_Flip_Flop t_ff_1 (.T(increment), .clk(CLK), .Q(out_4[0]), .Qn(t_ff_1_qn), .reset(out_4[2]), .preset(INP[0]));
  T_Flip_Flop t_ff_2 (.T(increment), .clk(t_ff_1_qn), .Q(out_4[1]), .Qn(t_ff_2_qn), .reset(out_4[2]), .preset(INP[2]));
  T_Flip_Flop t_ff_3 (.T(increment), .clk(t_ff_2_qn), .Q(out_4[2]), .Qn(t_ff_3_qn), .reset(out_4[2]), .preset(INP[1]));
  T_Flip_Flop t_ff_4 (.T(increment), .clk(t_ff_3_qn), .Q(out_4[3]), .reset(1'b1), .preset(INP[3]));  // open: Qn
endmodule
